# Fritzing sketch session02 (saved by Fritzing 0.9.2b)
breadboards: 1

parts:
  Bauteil1 = Arduino Nano (Rev3.0)
  Bauteil2 = Arduino Nano (Rev3.0)
  R3 = Resistor [tolerance=±5% resistance=220 package=THT]
  LED3 = LED - 5mm [color="Yellow (595nm)" package="5 mm [THT]"]

nets:
  N1: Bauteil1.GND, R3.Pin_0
  N2: Bauteil1.D2, Bauteil2.D3, LED3.anode
  N3: R3.Pin_1, LED3.cathode

notes:
  IUT is
  connected to PC.
  Test device
  is connected to PC.
