# Fritzing sketch session04 (saved by Fritzing 0.9.2b)
breadboards: 1

parts:
  Bauteil1 = Arduino Nano (Rev3.0)
  Bauteil2 = Arduino Nano (Rev3.0)
  R1 = Resistor [tolerance=±5% resistance=220 package=THT]
  LED1 = LED - 5mm [color="Yellow (595nm)" package="5 mm [THT]"]

nets:
  N1: Bauteil1.RESET, Bauteil2.D5
  N2: Bauteil1.GND, R1.Pin_0
  N3: Bauteil1.D2, Bauteil2.D3, LED1.anode
  N4: R1.Pin_1, LED1.cathode

notes:
  IUT is
  connected to PC.
  Test device
  is connected to PC.
